# Fritzing sketch pbmw (saved by Fritzing 0.9.4)
circuit board: 8.46667cm x 5.64444cm

parts:
  Part1 = Arduino Micro (Rev3)
  Part2 = Adafruit ADS1115 16Bit I2C ADC [part_number="Adafruit #1085"]

nets:
  N1: Part1.RXLED/SS, Part2.SCL
  GND: Part1.GND, Part2.GND
  N2: Part1.D2/SDA, Part2.ADDR
  N3: Part1.D3/SCL, Part2.SDA
  3V3: Part1.3V3, Part2.VDD

custom parts:
  Adafruit ADS1115 16Bit I2C ADC: For microcontrollers without an analog-to-digital converter or when you want a higher-precision ADC, the ADS1115 provides 16-bit precision at 860 samples/second over I2C. The chip can be configured as 4 single-ended input channels, or two differential channels. As a nice bonus, it even includes a programmable gain amplifier, up to x16, to help boost up smaller single/differential signals to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
